// Logisim project vending_machine.circ as structural Verilog
module show_commodity_shap (
  input  [7:0] \选择商品编号 ,
  input  CLK
);

  wire decoder_1_out0, decoder_1_out1, decoder_1_out2, decoder_1_out3, decoder_1_out4, decoder_1_out5,
       decoder_1_out6, decoder_1_out7, decoder_1_out8, decoder_1_out9, decoder_1_out10, decoder_1_out11,
       decoder_1_out12, decoder_1_out13, decoder_1_out14, decoder_1_out15, decoder_1_out16, decoder_1_out17,
       decoder_1_out18, decoder_1_out19, decoder_1_out20, decoder_1_out21, decoder_1_out22, decoder_1_out23,
       decoder_1_out24, decoder_1_out25, decoder_1_out26, decoder_1_out27, decoder_1_out28, decoder_1_out29,
       decoder_1_out30, decoder_1_out31;
  wire [4:0] goods_selection_1_out_4;
  wire [7:0] goods_selection_1_out_3;
  wire [31:0] register_1_q, register_2_q, register_3_q, register_4_q, register_5_q, register_6_q,
       register_7_q, register_8_q, register_9_q, register_10_q, register_11_q, register_12_q, register_13_q,
       register_14_q, register_15_q, register_16_q, register_17_q, register_18_q, register_19_q,
       register_20_q, register_21_q, register_22_q, register_23_q, register_24_q, register_25_q,
       register_26_q, register_27_q, register_28_q, register_29_q, register_30_q, register_31_q,
       register_32_q, rom_1_data;

  Goods_selection goods_selection_1 (
    .\选择商品编号 (\选择商品编号 ), .CLK(CLK), .out_3(goods_selection_1_out_3), .out_4(goods_selection_1_out_4));
  ROM #(.addrWidth(8), .dataWidth(32), .Select("low")) rom_1 (.addr(goods_selection_1_out_3), .data(rom_1_data));
  Decoder #(.select(5), .tristate("false"), .disabled(0), .enable("false")) decoder_1 (
    .out0(decoder_1_out0), .out1(decoder_1_out1), .out2(decoder_1_out2), .out3(decoder_1_out3),
    .out4(decoder_1_out4), .out5(decoder_1_out5), .out6(decoder_1_out6), .out7(decoder_1_out7),
    .out8(decoder_1_out8), .out9(decoder_1_out9), .out10(decoder_1_out10), .out11(decoder_1_out11),
    .out12(decoder_1_out12), .out13(decoder_1_out13), .out14(decoder_1_out14), .out15(decoder_1_out15),
    .out16(decoder_1_out16), .out17(decoder_1_out17), .out18(decoder_1_out18), .out19(decoder_1_out19),
    .out20(decoder_1_out20), .out21(decoder_1_out21), .out22(decoder_1_out22), .out23(decoder_1_out23),
    .out24(decoder_1_out24), .out25(decoder_1_out25), .out26(decoder_1_out26), .out27(decoder_1_out27),
    .out28(decoder_1_out28), .out29(decoder_1_out29), .out30(decoder_1_out30), .out31(decoder_1_out31),
    .sel(goods_selection_1_out_4));
  Register #(.width(32), .trigger("rising"), .Select("low")) register_1 (
    .D(rom_1_data), .en(decoder_1_out0), .Q(register_1_q), .clk(CLK), .cs(1'b0));  // open: clr, preset
  Register #(.width(32), .trigger("rising"), .Select("low")) register_2 (
    .D(rom_1_data), .en(decoder_1_out2), .Q(register_2_q), .clk(CLK), .cs(1'b0));  // open: clr, preset
  Register #(.width(32), .trigger("rising"), .Select("low")) register_3 (
    .D(rom_1_data), .en(decoder_1_out4), .Q(register_3_q), .clk(CLK), .cs(1'b0));  // open: clr, preset
  Register #(.width(32), .trigger("rising"), .Select("low")) register_4 (
    .D(rom_1_data), .en(decoder_1_out6), .Q(register_4_q), .clk(CLK), .cs(1'b0));  // open: clr, preset
  Register #(.width(32), .trigger("rising"), .Select("low")) register_5 (
    .D(rom_1_data), .en(decoder_1_out8), .Q(register_5_q), .clk(CLK), .cs(1'b0));  // open: clr, preset
  Register #(.width(32), .trigger("rising"), .Select("low")) register_6 (
    .D(rom_1_data), .en(decoder_1_out10), .Q(register_6_q), .clk(CLK), .cs(1'b0));  // open: clr, preset
  Register #(.width(32), .trigger("rising"), .Select("low")) register_7 (
    .D(rom_1_data), .en(decoder_1_out12), .Q(register_7_q), .clk(CLK), .cs(1'b0));  // open: clr, preset
  Register #(.width(32), .trigger("rising"), .Select("low")) register_8 (
    .D(rom_1_data), .en(decoder_1_out14), .Q(register_8_q), .clk(CLK), .cs(1'b0));  // open: clr, preset
  Register #(.width(32), .trigger("rising"), .Select("low")) register_9 (
    .D(rom_1_data), .en(decoder_1_out16), .Q(register_9_q), .clk(CLK), .cs(1'b0));  // open: clr, preset
  Register #(.width(32), .trigger("rising"), .Select("low")) register_10 (
    .D(rom_1_data), .en(decoder_1_out18), .Q(register_10_q), .clk(CLK), .cs(1'b0));  // open: clr, preset
  Register #(.width(32), .trigger("rising"), .Select("low")) register_11 (
    .D(rom_1_data), .en(decoder_1_out20), .Q(register_11_q), .clk(CLK), .cs(1'b0));  // open: clr, preset
  Register #(.width(32), .trigger("rising"), .Select("low")) register_12 (
    .D(rom_1_data), .en(decoder_1_out22), .Q(register_12_q), .clk(CLK), .cs(1'b0));  // open: clr, preset
  Register #(.width(32), .trigger("rising"), .Select("low")) register_13 (
    .D(rom_1_data), .en(decoder_1_out24), .Q(register_13_q), .clk(CLK), .cs(1'b0));  // open: clr, preset
  Register #(.width(32), .trigger("rising"), .Select("low")) register_14 (
    .D(rom_1_data), .en(decoder_1_out26), .Q(register_14_q), .clk(CLK), .cs(1'b0));  // open: clr, preset
  Register #(.width(32), .trigger("rising"), .Select("low")) register_15 (
    .D(rom_1_data), .en(decoder_1_out28), .Q(register_15_q), .clk(CLK), .cs(1'b0));  // open: clr, preset
  Register #(.width(32), .trigger("rising"), .Select("low")) register_16 (
    .D(rom_1_data), .en(decoder_1_out30), .Q(register_16_q), .clk(CLK), .cs(1'b0));  // open: clr, preset
  Register #(.width(32), .trigger("rising"), .Select("low")) register_17 (
    .D(rom_1_data), .en(decoder_1_out1), .Q(register_17_q), .clk(CLK), .cs(1'b0));  // open: clr, preset
  Register #(.width(32), .trigger("rising"), .Select("low")) register_18 (
    .D(rom_1_data), .en(decoder_1_out3), .Q(register_18_q), .clk(CLK), .cs(1'b0));  // open: clr, preset
  Register #(.width(32), .trigger("rising"), .Select("low")) register_19 (
    .D(rom_1_data), .en(decoder_1_out5), .Q(register_19_q), .clk(CLK), .cs(1'b0));  // open: clr, preset
  Register #(.width(32), .trigger("rising"), .Select("low")) register_20 (
    .D(rom_1_data), .en(decoder_1_out7), .Q(register_20_q), .clk(CLK), .cs(1'b0));  // open: clr, preset
  Register #(.width(32), .trigger("rising"), .Select("low")) register_21 (
    .D(rom_1_data), .en(decoder_1_out9), .Q(register_21_q), .clk(CLK), .cs(1'b0));  // open: clr, preset
  Register #(.width(32), .trigger("rising"), .Select("low")) register_22 (
    .D(rom_1_data), .en(decoder_1_out11), .Q(register_22_q), .clk(CLK), .cs(1'b0));  // open: clr, preset
  Register #(.width(32), .trigger("rising"), .Select("low")) register_23 (
    .D(rom_1_data), .en(decoder_1_out13), .Q(register_23_q), .clk(CLK), .cs(1'b0));  // open: clr, preset
  Register #(.width(32), .trigger("rising"), .Select("low")) register_24 (
    .D(rom_1_data), .en(decoder_1_out15), .Q(register_24_q), .clk(CLK), .cs(1'b0));  // open: clr, preset
  Register #(.width(32), .trigger("rising"), .Select("low")) register_25 (
    .D(rom_1_data), .en(decoder_1_out17), .Q(register_25_q), .clk(CLK), .cs(1'b0));  // open: clr, preset
  Register #(.width(32), .trigger("rising"), .Select("low")) register_26 (
    .D(rom_1_data), .en(decoder_1_out19), .Q(register_26_q), .clk(CLK), .cs(1'b0));  // open: clr, preset
  Register #(.width(32), .trigger("rising"), .Select("low")) register_27 (
    .D(rom_1_data), .en(decoder_1_out21), .Q(register_27_q), .clk(CLK), .cs(1'b0));  // open: clr, preset
  Register #(.width(32), .trigger("rising"), .Select("low")) register_28 (
    .D(rom_1_data), .en(decoder_1_out23), .Q(register_28_q), .clk(CLK), .cs(1'b0));  // open: clr, preset
  Register #(.width(32), .trigger("rising"), .Select("low")) register_29 (
    .D(rom_1_data), .en(decoder_1_out25), .Q(register_29_q), .clk(CLK), .cs(1'b0));  // open: clr, preset
  Register #(.width(32), .trigger("rising"), .Select("low")) register_30 (
    .D(rom_1_data), .en(decoder_1_out27), .Q(register_30_q), .clk(CLK), .cs(1'b0));  // open: clr, preset
  Register #(.width(32), .trigger("rising"), .Select("low")) register_31 (
    .D(rom_1_data), .en(decoder_1_out29), .Q(register_31_q), .clk(CLK), .cs(1'b0));  // open: clr, preset
  Register #(.width(32), .trigger("rising"), .Select("low")) register_32 (
    .D(rom_1_data), .en(decoder_1_out31), .Q(register_32_q), .clk(CLK), .cs(1'b0));  // open: clr, preset
  DotMatrix #(.inputtype("column"), .matrixcols(32), .matrixrows(32), .persist(0), .dotshape("square")) dotmatrix_1 (
    .col0(register_1_q), .col1(register_17_q), .col2(register_2_q), .col3(register_18_q),
    .col4(register_3_q), .col5(register_19_q), .col6(register_4_q), .col7(register_20_q),
    .col8(register_5_q), .col9(register_21_q), .col10(register_6_q), .col11(register_22_q),
    .col12(register_7_q), .col13(register_23_q), .col14(register_8_q), .col15(register_24_q),
    .col16(register_9_q), .col17(register_25_q), .col18(register_10_q), .col19(register_26_q),
    .col20(register_11_q), .col21(register_27_q), .col22(register_12_q), .col23(register_28_q),
    .col24(register_13_q), .col25(register_29_q), .col26(register_14_q), .col27(register_30_q),
    .col28(register_15_q), .col29(register_31_q), .col30(register_16_q), .col31(register_32_q));

  // Notes on the sheet:
  //   contents of rom_1 (hex, n*v repeats v):
  //   11*0 1ffffe 3e827e3 7f882003 90082003 80082003 80002003 98002003 ff882003 3f87fe3 3ffffe 3800c
endmodule

module Goods_selection (
  input  [7:0] \选择商品编号 ,
  input  CLK,
  output [7:0] out_3,
  output [4:0] out_4
);

  wire comparator_1_eq, comparator_1_gt, comparator_2_gt, comparator_3_eq, not_1_out, not_2_out, or_1_out,
       or_2_out;
  wire [7:0] adder_1_out, multiplier_1_out;

  Multiplier #(.width(8)) multiplier_1 (.a(\选择商品编号 ), .b(8'h20), .out(multiplier_1_out));  // open: cin, cout
  Adder #(.width(8)) adder_1 (.a(multiplier_1_out), .b(8'h20), .out(adder_1_out), .cin(1'b0));  // open: cout
  not not_1 (not_1_out, 1'b0);
  not not_2 (not_2_out, 1'b0);
  Counter #(.width(8), .max('hff), .ongoal("wrap"), .trigger("rising"), .behavior("new")) counter_1 (
    .load(or_2_out), .D(multiplier_1_out), .count(not_1_out), .Q(out_3), .clk(CLK), .clr(1'b0),
    .preset(1'b0), .down(1'b0));  // open: carry
  Comparator #(.width(8), .mode("twosComplement")) comparator_1 (
    .a(out_3), .b(adder_1_out), .gt(comparator_1_gt), .eq(comparator_1_eq));  // open: lt
  Comparator #(.width(8), .mode("twosComplement")) comparator_2 (
    .a(multiplier_1_out), .b(out_3), .gt(comparator_2_gt));  // open: eq, lt
  Comparator #(.width(8), .mode("twosComplement")) comparator_3 (
    .a({8{1'b0}}), .b(out_3), .eq(comparator_3_eq));  // open: gt, lt
  Counter #(.width(5), .max('h1f), .ongoal("wrap"), .trigger("rising"), .behavior("new")) counter_2 (
    .load(1'b0), .count(not_2_out), .Q(out_4), .clk(CLK), .clr(or_2_out), .preset(1'b0), .down(1'b0));  // open: D, carry
  or or_1 (or_1_out, comparator_1_gt, comparator_1_eq);
  or or_2 (or_2_out, or_1_out, comparator_2_gt, comparator_3_eq);

  // Notes on the sheet:
  //   结束地址
  //   地址寄存器
  //   点阵寄存器
  //   大于等于结束地址
  //   小于开始地址
  //   等于0地址
endmodule
